// Logisim project processor_modified.circ as structural Verilog
module ALU (
  input  [2:0] F,
  input  [31:0] B,
  input  [31:0] A,
  output Zero,
  output [31:0] Y
);

  wire [31:0] adder_1_out, and_1_out, bit_extender_1_out, multiplexer_1_out, not_1_out, or_1_out;

  assign not_1_out = ~B;  // NOT_Gate not_1, 32 bits wide
  Multiplexer #(.width(32), .enable("false")) multiplexer_1 (
    .in0(B), .in1(not_1_out), .out(multiplexer_1_out), .sel(F[2]));
  Adder #(.width(32)) adder_1 (.a(multiplexer_1_out), .b(A), .out(adder_1_out), .cin(F[2]));  // open: cout
  assign and_1_out = multiplexer_1_out & A;  // AND_Gate and_1, 32 bits wide
  assign or_1_out = multiplexer_1_out | A;  // OR_Gate or_1, 32 bits wide
  assign bit_extender_1_out = {{31{1'b0}}, adder_1_out[31]};  // Bit_Extender bit_extender_1
  Multiplexer #(.select(2), .width(32), .enable("false")) multiplexer_2 (
    .in0(and_1_out), .in1(or_1_out), .in2(adder_1_out), .in3(bit_extender_1_out), .out(Y), .sel(F[1:0]));
  _32_to_1_NOR _32_to_1__NOR (.Input(Y), .Output(Zero));
endmodule

module Datapath (
  output [31:0] Y,
  output [7:0] Y_2,
  output [7:0] Y_3,
  output [2:0] Y_4,
  output [7:0] Y_5,
  output [2:0] Y_6,
  output [31:0] Y_7,
  output [7:0] Y_8,
  output [7:0] Y_9,
  output [2:0] Y_10,
  output [31:0] Y_11,
  output [15:0] Y_12
);

  wire alu_1_zero, and_1_out, clock_1_out, controlunit_1_alusrc, controlunit_1_branch, controlunit_1_regdst,
       controlunit_1_regwrite;
  wire [2:0] controlunit_1_alucontrol, multiplexer_2_out;
  wire [7:0] adder_1_out, adder_2_out, bit_extender_2_out, multiplexer_1_out, register_1_q, shifter_1_out,
       shifter_4_out;
  wire [31:0] multiplexer_3_out, registerfile_1_rd1, registerfile_1_rd2;

  Clock clock_1 (.out(clock_1_out));
  Multiplexer #(.width(8), .enable("false")) multiplexer_1 (
    .in0(adder_1_out), .in1(adder_2_out), .out(multiplexer_1_out), .sel(and_1_out));
  Register register_1 (.D(multiplexer_1_out), .Q(register_1_q), .clk(clock_1_out));  // open: en, clr
  Adder adder_1 (.a(8'h4), .b(register_1_q), .out(adder_1_out));  // open: cin, cout
  Shifter #(.shift("lr")) shifter_1 (.in(register_1_q), .\dist (3'b010), .out(shifter_1_out));
  ROM #(.dataWidth(32)) rom_1 (.addr(shifter_1_out), .data(Y));  // open: sel
  Adder adder_2 (.a(adder_1_out), .b(shifter_4_out), .out(adder_2_out));  // open: cin, cout
  BitSelector #(.width(32), .group(16)) bitselector_1 (.in(Y), .out(Y_12), .sel(1'b0));
  ControlUnit controlunit_1 (
    .Instruction(Y), .RegDst(controlunit_1_regdst), .RegWrite(controlunit_1_regwrite),
    .ALUControl(controlunit_1_alucontrol), .Branch(controlunit_1_branch), .ALUSrc(controlunit_1_alusrc));
  BitSelector #(.width(32), .group(8)) bitselector_2 (.in(Y), .out(Y_2), .sel(2'b10));
  BitSelector #(.width(32), .group(8)) bitselector_3 (.in(Y), .out(Y_5), .sel(2'b10));
  BitSelector #(.width(32), .group(8)) bitselector_4 (.in(Y), .out(Y_9), .sel(2'b01));
  Shifter #(.shift("lr")) shifter_2 (.in(Y_2), .\dist (3'b101), .out(Y_3));
  Shifter #(.shift("lr")) shifter_3 (.in(Y_9), .\dist (3'b011), .out(Y_8));
  BitSelector #(.group(3)) bitselector_5 (.in(Y_3), .out(Y_4), .sel(2'b00));
  BitSelector #(.group(3)) bitselector_6 (.in(Y_5), .out(Y_6), .sel(2'b00));
  BitSelector #(.group(3)) bitselector_7 (.in(Y_8), .out(Y_10), .sel(2'b00));
  assign Y_11 = {{16{Y_12[15]}}, Y_12};  // Bit_Extender bit_extender_1
  Multiplexer #(.width(3), .enable("false")) multiplexer_2 (
    .in0(Y_6), .in1(Y_10), .out(multiplexer_2_out), .sel(controlunit_1_regdst));
  Bit_Extender #(.in_width(32), .out_width(8), .\type ("sign")) bit_extender_2 (.in(Y_11), .out(bit_extender_2_out));
  RegisterFile registerfile_1 (
    .A1(Y_4), .WD(Y_7), .A2(Y_6), .WE(controlunit_1_regwrite), .RD1(registerfile_1_rd1),
    .RD2(registerfile_1_rd2), .A3(multiplexer_2_out), .CLK(clock_1_out));  // open: V0
  Shifter shifter_4 (.in(bit_extender_2_out), .\dist (3'b010), .out(shifter_4_out));
  Multiplexer #(.width(32), .enable("false")) multiplexer_3 (
    .in0(registerfile_1_rd2), .in1(Y_11), .out(multiplexer_3_out), .sel(controlunit_1_alusrc));
  ALU alu_1 (.F(controlunit_1_alucontrol), .B(multiplexer_3_out), .A(registerfile_1_rd1), .Y(Y_7), .Zero(alu_1_zero));
  and and_1 (and_1_out, controlunit_1_branch, alu_1_zero);

  // Notes on the sheet:
  //   PC
  //   instruction memory
  //   contents of rom_1 (hex, n*v repeats v):
  //   20040004 20820002 441020 10440002 2042fffd 1000fffd 20
  //   16,17,18,19,20 = 5 bits
  //   16,17,18 = 3 bits
  //   11,12,13,14,15 = 5 bits
  //   11,12,13 = 3 bits
  //   4*imm
  //   since our register file takes 3 bits we take the 3 LS bits of the 5 mips rt bits for A1
  //   21,22...25 = 5 bits
  //   23,22,21 = 3 bits
  //   We dont have a MemToReg since we dont use non-register memory
  //   Data Memory is the non-register memory / memory outside of the processor - we dont use it here
endmodule

module Tests (
  output [31:0] Y,
  output [7:0] out_2,
  output [7:0] out_3,
  output [2:0] out_4
);

  BitSelector #(.width(32), .group(8)) bitselector_1 (.in(32'h12356789), .out(out_2), .sel(2'b01));
  BitSelector #(.width(32), .group(8)) bitselector_2 (.in(32'h12356789), .out(out_3), .sel(2'b01));
  BitSelector #(.group(3)) bitselector_3 (.in(out_3), .out(out_4), .sel(2'b00));

  assign Y = 32'h12356789;

  // Notes on the sheet:
  //   binary values in Logisim. Convince yourself how the bits are displayed.
  //   Example 2: The bit selector is configured to have 32  
  //   bit group #1 (starting at index 0) is selected for the output.
  //   That is, the 8 bits 0x67 at bit indices 15..8  are sent to the output.
  //   Example 3: Now, assume that you want to extract 3 bits at   
  //   Example 1: A simple example that illustrates how 32-bit values are displayed as 
  //   input bits and 8 output bits. The parameter constant is 1, which means that   
  //   bit indices 10..8. This can be accoplished by putting two bit selecotrs in series.
endmodule

module RegisterFile (
  input  CLK,
  input  [2:0] A1,
  input  [31:0] WD,
  input  [2:0] A2,
  input  WE,
  input  [2:0] A3,
  output [31:0] RD1,
  output [31:0] RD2,
  output [31:0] V0
);

  wire and_1_out, and_2_out, and_3_out, and_4_out, and_5_out, and_6_out, and_7_out, and_8_out,
       decoder_1_out0, decoder_1_out1, decoder_1_out2, decoder_1_out3, decoder_1_out4, decoder_1_out5,
       decoder_1_out6, decoder_1_out7;
  wire [31:0] register_1_q, register_2_q, register_4_q, register_5_q, register_6_q, register_7_q,
       register_8_q;

  Decoder #(.select(3)) decoder_1 (
    .out0(decoder_1_out0), .out1(decoder_1_out1), .out2(decoder_1_out2), .out3(decoder_1_out3),
    .out4(decoder_1_out4), .out5(decoder_1_out5), .out6(decoder_1_out6), .out7(decoder_1_out7), .sel(A3));  // open: en
  and and_1 (and_1_out, 1'b0, decoder_1_out0);
  and and_2 (and_2_out, WE, decoder_1_out1);
  and and_3 (and_3_out, WE, decoder_1_out2);
  and and_4 (and_4_out, WE, decoder_1_out3);
  and and_5 (and_5_out, WE, decoder_1_out4);
  and and_6 (and_6_out, WE, decoder_1_out5);
  and and_7 (and_7_out, WE, decoder_1_out6);
  and and_8 (and_8_out, WE, decoder_1_out7);
  Register #(.width(32)) register_1 (.en(and_1_out), .Q(register_1_q), .clk(CLK));  // open: D, clr
  Register #(.width(32)) register_2 (.D(WD), .en(and_2_out), .Q(register_2_q), .clk(CLK));  // open: clr
  Register #(.width(32)) register_3 (.D(WD), .en(and_3_out), .Q(V0), .clk(CLK));  // open: clr
  Register #(.width(32)) register_4 (.D(WD), .en(and_4_out), .Q(register_4_q), .clk(CLK));  // open: clr
  Register #(.width(32)) register_5 (.D(WD), .en(and_5_out), .Q(register_5_q), .clk(CLK));  // open: clr
  Register #(.width(32)) register_6 (.D(WD), .en(and_6_out), .Q(register_6_q), .clk(CLK));  // open: clr
  Register #(.width(32)) register_7 (.D(WD), .en(and_7_out), .Q(register_7_q), .clk(CLK));  // open: clr
  Register #(.width(32)) register_8 (.D(WD), .en(and_8_out), .Q(register_8_q), .clk(CLK));  // open: clr
  Multiplexer #(.select(3), .width(32)) multiplexer_1 (
    .in0(register_1_q), .in1(register_2_q), .in2(V0), .in3(register_4_q), .in4(register_5_q),
    .in5(register_6_q), .in6(register_7_q), .in7(register_8_q), .out(RD1), .sel(A1));  // open: en
  Multiplexer #(.select(3), .width(32)) multiplexer_2 (
    .in0(register_1_q), .in1(register_2_q), .in2(V0), .in3(register_4_q), .in4(register_5_q),
    .in5(register_6_q), .in6(register_7_q), .in7(register_8_q), .out(RD2), .sel(A2));  // open: en

  // Notes on the sheet:
  //   write adress
  //   write enable (toggle R/W)
  //   clock
  //   write input
  //   $0
  //   $at
  //   adress 1
  //   adress 2
  //   $v0
  //   $v1
  //   $a0
  //   $a1
  //   $a2
  //   $a3
  //   register på adress 1
  //   register på adress 2
endmodule

module ControlUnit (
  input  [31:0] Instruction,
  output RegDst,
  output RegWrite,
  output ALUSrc,
  output Branch,
  output [2:0] ALUControl
);

  wire [1:0] multiplexer_1_out;
  wire [5:0] bitselector_1_out, bitselector_2_out;
  wire [31:0] shifter_1_out;

  Shifter #(.width(32), .shift("lr")) shifter_1 (.in(Instruction), .\dist (5'b11010), .out(shifter_1_out));
  BitSelector #(.width(32), .group(6)) bitselector_1 (.in(Instruction), .out(bitselector_1_out), .sel(3'b000));
  BitSelector #(.width(32), .group(6)) bitselector_2 (.in(shifter_1_out), .out(bitselector_2_out), .sel(3'b000));
  ALUDecoder ALUDecoder (.funct(bitselector_1_out), .ALUOp(multiplexer_1_out), .ALUControl(ALUControl));
  Comparator #(.width(6), .mode("unsigned")) comparator_1 (
    .a(bitselector_2_out), .b(6'b001000), .eq(ALUSrc));  // open: gt, lt
  Comparator #(.width(6), .mode("unsigned")) comparator_2 (
    .a(bitselector_2_out), .b({6{1'b0}}), .eq(RegDst));  // open: gt, lt
  Comparator #(.width(6), .mode("unsigned")) comparator_3 (
    .a(bitselector_2_out), .b(6'b000100), .eq(Branch));  // open: gt, lt
  Multiplexer #(.select(3), .width(2)) multiplexer_1 (
    .in1(2'b00), .in2(2'b10), .in4(2'b01), .out(multiplexer_1_out), .sel({Branch, RegDst, ALUSrc}));  // open: in0, in3, in5, in6, in7, en
  or or_1 (RegWrite, ALUSrc, RegDst);

  // Notes on the sheet:
  //   funct
  //   if op == 8
  //   if op == 0
  //   if op==4
  //   beq,add,addi
  //   addi
  //   add
  //   beq
  //   ALUOp
endmodule

module _32_to_1_NOR (
  input  [31:0] Input,
  output Output
);

  nor nor_1 (Output, Input[0], Input[1], Input[2], Input[3], Input[4], Input[5], Input[6], Input[7], Input[8], Input[9], Input[10], Input[11], Input[12], Input[13], Input[14], Input[15], Input[16], Input[17], Input[18], Input[19], Input[20], Input[21], Input[22], Input[23], Input[24], Input[25], Input[26], Input[27], Input[28], Input[29], Input[30], Input[31]);
endmodule

module test (
);

  wire alu_1_zero, undriven;
  wire [2:0] undriven_2;
  wire [31:0] registerfile_1_rd1, rom_1_data;

  ROM #(.addrWidth(3), .dataWidth(32)) rom_1 (.data(rom_1_data));  // open: addr, sel
  RegisterFile registerfile_1 (.WE(undriven), .RD1(registerfile_1_rd1));  // open: A1, WD, A2, RD2, A3, V0, CLK
  ALU alu_1 (.F(undriven_2), .A(registerfile_1_rd1), .Zero(alu_1_zero));  // open: B, Y
  // AND_Gate and_1 has open pins: in4=alu_1_zero, out=open

  // Notes on the sheet:
  //   Reg Write
  //   ALU Control
endmodule

module ALUDecoder (
  input  [1:0] ALUOp,
  input  [5:0] funct,
  output [2:0] ALUControl
);

  wire comparator_1_eq, comparator_2_eq, comparator_3_eq, comparator_4_eq, comparator_5_eq, comparator_6_eq,
       comparator_7_eq;
  wire [2:0] multiplexer_1_out, multiplexer_3_out;
  wire [4:0] and_1_out;

  Comparator #(.width(3), .mode("unsigned")) comparator_1 (
    .a(funct[5:3]), .b(3'b100), .eq(comparator_1_eq));  // open: gt, lt
  Comparator #(.width(3), .mode("unsigned")) comparator_2 (
    .a(funct[5:3]), .b(3'b101), .eq(comparator_2_eq));  // open: gt, lt
  Comparator #(.width(3), .mode("unsigned")) comparator_3 (
    .a(funct[2:0]), .b(3'b000), .eq(comparator_3_eq));  // open: gt, lt
  Comparator #(.width(3), .mode("unsigned")) comparator_4 (
    .a(funct[2:0]), .b(3'b010), .eq(comparator_4_eq));  // open: gt, lt
  Comparator #(.width(3), .mode("unsigned")) comparator_5 (
    .a(funct[2:0]), .b(3'b100), .eq(comparator_5_eq));  // open: gt, lt
  Comparator #(.width(3), .mode("unsigned")) comparator_6 (
    .a(funct[2:0]), .b(3'b101), .eq(comparator_6_eq));  // open: gt, lt
  Multiplexer #(.select(2), .width(3), .enable("false")) multiplexer_1 (
    .in0(3'b010), .in1(3'b110), .out(multiplexer_1_out), .sel(ALUOp));  // open: in2, in3
  and and_1 (and_1_out[0], comparator_1_eq, comparator_3_eq);
  and and_2 (and_1_out[1], comparator_1_eq, comparator_4_eq);
  and and_3 (and_1_out[2], comparator_1_eq, comparator_5_eq);
  and and_4 (and_1_out[3], comparator_1_eq, comparator_6_eq);
  and and_5 (and_1_out[4], comparator_2_eq, comparator_4_eq);
  Comparator #(.width(2), .mode("unsigned")) comparator_7 (.a(ALUOp), .b(2'b10), .eq(comparator_7_eq));  // open: gt, lt
  Multiplexer #(.width(3), .enable("false")) multiplexer_2 (
    .in0(multiplexer_1_out), .in1(multiplexer_3_out), .out(ALUControl), .sel(comparator_7_eq));
  Multiplexer #(.select(5), .width(3), .enable("false")) multiplexer_3 (
    .in1(3'b010), .in2(3'b110), .in4(3'b000), .in8(3'b001), .in16(3'b111), .out(multiplexer_3_out),
    .sel(and_1_out));  // open: in0, in3, in5, in6, in7, in9, in10, in11, in12, in13, in14, in15, in17, in18, in19, in20, in21, in22, in23, in24, in25, in26, in27, in28, in29, in30, in31

  // Notes on the sheet:
  //   first 3 bits
  //   next 3 bits
  //   010(add)
  //   110(subtract)
  //   ==100
  //   ==101
  //   ==000
  //   ==010
  //   ==100
  //   ==101
  //   ==100 000
  //   ==100 010
  //   ==100 100
  //   ==100 101
  //   ==101 010
  //   ALUOp == 10 look at funct
endmodule
